// Logisim project GR8CPUr2.circ as structural Verilog: 7 circuits, main circuit main
// GR8CPU
module main (
);

  wire ACR, ACR_out, ADA, ADA_out, ADC, ADC_out, adder_1_cout, AIA, AIA_out, AIB, AIB_out, AIO, AIO_out, ALO,
       ALO_out, and_1_out, and_2_out, and_4_out, and_5_out, and_6_out, and_8_out, and_9_out, and_10_out,
       BROKEN_out, buffer_4_out, buffer_5_out, buffer_6_out, buffer_9_out, button_1_out, button_2_out,
       button_3_out, button_4_out, button_5_out, button_6_out, button_7_out, button_8_out, button_9_out,
       button_10_out, button_11_out, button_12_out, button_13_out, button_14_out, button_15_out,
       button_16_out, button_17_out, button_18_out, button_19_out, button_20_out, button_21_out,
       button_22_out, button_23_out, button_24_out, button_25_out, button_26_out, button_27_out,
       button_28_out, button_29_out, button_30_out, CIN, CIN_out, clock_1_out, clock_2_clock_out,
       clock_2_green_out, clock_2_red_out, COB, COB_out, comparator_1_eq, decoder_1_out0, decoder_1_out1,
       decoder_1_out2, decoder_1_out3, FRBC, FRI, FRI_out, HLT, HLT_out, ILD, ILD_out, IRI, IRI_out, ISA,
       ISA_out, IST, IST_out, JBC, JBC_out, JMP, JMP_out, manual_write_out, n8_bit_enter_o_mat_1_out_10,
       n8_bit_enter_o_mat_1_out_11, n8_bit_enter_o_mat_1_out_12, n8_bit_enter_o_mat_1_out_13,
       n8_bit_enter_o_mat_1_out_14, n8_bit_enter_o_mat_1_out_15, n8_bit_enter_o_mat_1_out_16,
       n8_bit_enter_o_mat_1_out_17, n8_bit_enter_o_mat_2_out_10, n8_bit_enter_o_mat_2_out_11,
       n8_bit_enter_o_mat_2_out_12, n8_bit_enter_o_mat_2_out_13, n8_bit_enter_o_mat_2_out_14,
       n8_bit_enter_o_mat_2_out_15, n8_bit_enter_o_mat_2_out_16, n8_bit_enter_o_mat_2_out_17,
       n8_bit_enter_o_mat_3_out_10, n8_bit_enter_o_mat_3_out_11, n8_bit_enter_o_mat_3_out_12,
       n8_bit_enter_o_mat_3_out_13, n8_bit_enter_o_mat_3_out_14, n8_bit_enter_o_mat_3_out_15,
       n8_bit_enter_o_mat_3_out_16, n8_bit_enter_o_mat_3_out_17, n8_bit_enter_o_mat_4_out_10,
       n8_bit_enter_o_mat_4_out_11, n8_bit_enter_o_mat_4_out_12, n8_bit_enter_o_mat_4_out_13,
       n8_bit_enter_o_mat_4_out_14, n8_bit_enter_o_mat_4_out_15, n8_bit_enter_o_mat_4_out_16,
       n8_bit_enter_o_mat_4_out_17, n8_bit_enter_o_mat_5_out_10, n8_bit_enter_o_mat_5_out_11,
       n8_bit_enter_o_mat_5_out_12, n8_bit_enter_o_mat_5_out_13, n8_bit_enter_o_mat_5_out_14,
       n8_bit_enter_o_mat_5_out_15, n8_bit_enter_o_mat_5_out_16, n8_bit_enter_o_mat_5_out_17,
       n8_bit_enter_o_mat_6_out_10, n8_bit_enter_o_mat_6_out_11, n8_bit_enter_o_mat_6_out_12,
       n8_bit_enter_o_mat_6_out_13, n8_bit_enter_o_mat_6_out_14, n8_bit_enter_o_mat_6_out_15,
       n8_bit_enter_o_mat_6_out_16, n8_bit_enter_o_mat_6_out_17, nand_1_out, nand_2_out, nand_3_out,
       nand_4_out, nand_5_out, nand_6_out, nand_7_out, nand_8_out, nand_9_out, NC_2_out, NC_3_out, NC_out,
       nor_1_out, nor_2_out, nor_3_out, nor_4_out, not_1_out, not_2_out, not_3_out, not_4_out, not_5_out,
       not_6_out, not_7_out, not_8_out, OP0_out, OP1_out, OP2_out, OPTN0, OPTN1, OPTN2, or_1_out, or_6_out,
       or_7_out, or_9_out, or_10_out, or_11_out, or_12_out, or_13_out, or_14_out, or_15_out, or_16_out,
       or_17_out, or_22_out, pull_resistor_4_node, pull_resistor_5_node, pull_resistor_7_node,
       ram_select_o_mat_1_green_led_out, ram_select_o_mat_1_load_clock, ram_select_o_mat_1_red_led_out,
       ram_select_o_mat_1_write_out, RESET_2_out, RESET_out, RIA, RIA_out, RIB, RIB_out, RIC, RIC_out, RID,
       RID_out, ROA, ROA_out, ROB, ROB_out, ROC, ROC_out, ROD, ROD_out, RSTB, STR, STR_out, undriven,
       xor_1_out, xor_2_out;
  wire [1:0] alu_1_flags, register_5_q;
  wire [2:0] counter_1_q;
  wire [2:2] adder_1_out;
  wire [3:0] counter_3_q;
  wire [6:0] buffer_8_out;
  wire [7:0] adder_1_out_2, alu_1_out, buffer_7_out, controlled_buffer_3_out, counter_2_q,
       n8_bit_enter_o_mat_5_out, n8_bit_enter_o_mat_6_out, or_19_out, pull_resistor_3_node, ram_1_data,
       ram_select_o_mat_1_adress_out, ram_select_o_mat_1_data_out, ram_select_o_mat_1_rom_adress,
       register_1_q, register_3_q, register_4_q, register_6_q, rom_2_data, rom_3_data;
  wire [7:6] register_2_q;
  wire [7:7] buffer_8_out_2;
  wire [30:15] rom_1_data;
  wire [31:0] n8_bit_enter_o_mat_1_out, pull_resistor_9_node, register_7_q;

  Button u_RIB (.out(RIB_out));
  Button u_RIA (.out(RIA_out));
  LED led_1 (.in(n8_bit_enter_o_mat_1_out_10));
  LED led_2 (.in(n8_bit_enter_o_mat_1_out_11));
  Button u_FRI (.out(FRI_out));
  Button NC (.out(NC_out));
  LED led_3 (.in(n8_bit_enter_o_mat_2_out_10));
  LED led_4 (.in(n8_bit_enter_o_mat_2_out_11));
  Button u_JMP (.out(JMP_out));
  Button u_HLT (.out(HLT_out));
  LED led_5 (.in(n8_bit_enter_o_mat_3_out_10));
  LED led_6 (.in(n8_bit_enter_o_mat_3_out_11));
  Button NC_2 (.out(NC_2_out));
  Button NC_3 (.out(NC_3_out));
  LED led_7 (.in(n8_bit_enter_o_mat_4_out_10));
  LED led_8 (.in(n8_bit_enter_o_mat_4_out_11));
  Clock clock_1 (.out(clock_1_out));
  Button manual_write (.out(manual_write_out));
  Button BROKEN (.out(BROKEN_out));
  Button button_1 (.out(button_1_out));
  LED led_9 (.in(n8_bit_enter_o_mat_5_out_10));
  Button button_2 (.out(button_2_out));
  LED led_10 (.in(n8_bit_enter_o_mat_6_out_10));
  and and_1 (and_1_out, counter_1_q[1], counter_1_q[0]);
  LED led_11 (.in(adder_1_cout));
  Button u_ALO (.out(ALO_out));
  Button u_ACR (.out(ACR_out));
  Button u_AIO (.out(AIO_out));
  Button OP0 (.out(OP0_out));
  LED led_12 (.in(n8_bit_enter_o_mat_1_out_15));
  LED led_13 (.in(n8_bit_enter_o_mat_1_out_12));
  LED led_14 (.in(n8_bit_enter_o_mat_1_out_14));
  LED led_15 (.in(n8_bit_enter_o_mat_1_out_13));
  Button u_ROA (.out(ROA_out));
  Button u_ROD (.out(ROD_out));
  Button u_ROB (.out(ROB_out));
  Button u_ROC (.out(ROC_out));
  LED led_16 (.in(n8_bit_enter_o_mat_2_out_13));
  LED led_17 (.in(n8_bit_enter_o_mat_2_out_14));
  LED led_18 (.in(n8_bit_enter_o_mat_2_out_12));
  LED led_19 (.in(n8_bit_enter_o_mat_2_out_15));
  Button u_ILD (.out(ILD_out));
  Button u_COB (.out(COB_out));
  Button u_CIN (.out(CIN_out));
  Button u_IST (.out(IST_out));
  LED led_20 (.in(n8_bit_enter_o_mat_3_out_14));
  LED led_21 (.in(n8_bit_enter_o_mat_3_out_13));
  LED led_22 (.in(n8_bit_enter_o_mat_3_out_12));
  LED led_23 (.in(n8_bit_enter_o_mat_3_out_15));
  Button u_ADA (.out(ADA_out));
  Button u_ADC (.out(ADC_out));
  Button OP1 (.out(OP1_out));
  Button u_IRI (.out(IRI_out));
  LED led_24 (.in(n8_bit_enter_o_mat_4_out_15));
  LED led_25 (.in(n8_bit_enter_o_mat_4_out_12));
  LED led_26 (.in(n8_bit_enter_o_mat_4_out_13));
  LED led_27 (.in(n8_bit_enter_o_mat_4_out_14));
  Pull_Resistor pull_resistor_1 (.node(HLT));
  Button button_3 (.out(button_3_out));
  Button button_4 (.out(button_4_out));
  LED led_28 (.in(ram_select_o_mat_1_green_led_out));
  RAM_select_o_mat ram_select_o_mat_1 (
    .write(IST), .manual_write(manual_write_out), .adress(register_1_q), .data(controlled_buffer_3_out),
    .manual_adress(n8_bit_enter_o_mat_5_out), .manual_data(n8_bit_enter_o_mat_6_out), .auto(button_3_out),
    .green_led_out(ram_select_o_mat_1_green_led_out), .manual(button_4_out),
    .red_led_out(ram_select_o_mat_1_red_led_out), .write_out(ram_select_o_mat_1_write_out),
    .adress_out(ram_select_o_mat_1_adress_out), .data_out(ram_select_o_mat_1_data_out),
    .ROM_data(rom_2_data), .ROM_adress(ram_select_o_mat_1_rom_adress), .load(BROKEN_out),
    .load_clock(ram_select_o_mat_1_load_clock));
  LED led_29 (.in(ram_select_o_mat_1_red_led_out));
  Button button_5 (.out(button_5_out));
  Button button_6 (.out(button_6_out));
  Button button_7 (.out(button_7_out));
  Button button_8 (.out(button_8_out));
  LED led_30 (.in(n8_bit_enter_o_mat_5_out_12));
  LED led_31 (.in(n8_bit_enter_o_mat_5_out_11));
  LED led_32 (.in(n8_bit_enter_o_mat_5_out_13));
  LED led_33 (.in(n8_bit_enter_o_mat_5_out_14));
  Button button_9 (.out(button_9_out));
  Button button_10 (.out(button_10_out));
  Button button_11 (.out(button_11_out));
  Button button_12 (.out(button_12_out));
  LED led_34 (.in(n8_bit_enter_o_mat_6_out_11));
  LED led_35 (.in(n8_bit_enter_o_mat_6_out_13));
  LED led_36 (.in(n8_bit_enter_o_mat_6_out_12));
  LED led_37 (.in(n8_bit_enter_o_mat_6_out_14));
  DotMatrix #(.inputtype("row"), .matrixcols(3), .matrixrows(1), .dotshape("circle")) dotmatrix_1 (.row0(counter_1_q));
  or or_1 (or_1_out, and_4_out, pull_resistor_5_node);
  Counter #(.width(3), .max('h7), .trigger("falling")) counter_1 (
    .Q(counter_1_q), .clk(clock_2_clock_out), .clr(or_1_out));  // open: load, D, count, carry
  nor nor_1 (nor_1_out, counter_1_q[2], and_1_out);
  and and_2 (and_2_out, nor_1_out, not_1_out);
  not not_1 (not_1_out, counter_1_q[0]);
  and and_3 (IRI, nor_1_out, counter_1_q[0]);
  ROM #(.dataWidth(32)) rom_1 (
    .addr(adder_1_out_2),
    .data({RSTB, rom_1_data[30], OPTN1, ADA, ADC, rom_1_data[26], STR, JBC, JMP, rom_1_data[22:20], IST, rom_1_data[18:17], OPTN2, rom_1_data[15], FRI, ROD, ROC, ROB, ROA, RID, RIC, RIB, RIA, ALO, OPTN0, ACR, AIO, AIB, AIA}),
    .sel(adder_1_cout));
  Pull_Resistor pull_resistor_2 (.node({RSTB, rom_1_data[30], OPTN1, ADA, ADC, rom_1_data[26], STR, JBC, JMP, rom_1_data[22:20], IST, rom_1_data[18:17], OPTN2, rom_1_data[15], FRI, ROD, ROC, ROB, ROA, RID, RIC, RIB, RIA, ALO, OPTN0, ACR, AIO, AIB, AIA}));
  _8_bit_enter_o_mat u_8_bit_enter_o_mat_1 (
    .out(n8_bit_enter_o_mat_1_out[7:0]), .in_1(RIB_out), .out_10(n8_bit_enter_o_mat_1_out_10),
    .in_2(RIA_out), .out_11(n8_bit_enter_o_mat_1_out_11), .in_3(ALO_out),
    .out_12(n8_bit_enter_o_mat_1_out_12), .in_4(OP0_out), .out_13(n8_bit_enter_o_mat_1_out_13),
    .in_5(ACR_out), .out_14(n8_bit_enter_o_mat_1_out_14), .in_6(AIO_out),
    .out_15(n8_bit_enter_o_mat_1_out_15), .in_7(AIB_out), .out_16(n8_bit_enter_o_mat_1_out_16),
    .in_8(AIA_out), .out_17(n8_bit_enter_o_mat_1_out_17), .in_9(and_6_out));
  Button u_AIA (.out(AIA_out));
  Button u_AIB (.out(AIB_out));
  LED led_38 (.in(n8_bit_enter_o_mat_1_out_16));
  LED led_39 (.in(n8_bit_enter_o_mat_1_out_17));
  Button u_RID (.out(RID_out));
  _8_bit_enter_o_mat u_8_bit_enter_o_mat_2 (
    .out(n8_bit_enter_o_mat_1_out[15:8]), .in_1(NC_out), .out_10(n8_bit_enter_o_mat_2_out_10),
    .in_2(FRI_out), .out_11(n8_bit_enter_o_mat_2_out_11), .in_3(ROD_out),
    .out_12(n8_bit_enter_o_mat_2_out_12), .in_4(ROC_out), .out_13(n8_bit_enter_o_mat_2_out_13),
    .in_5(ROB_out), .out_14(n8_bit_enter_o_mat_2_out_14), .in_6(ROA_out),
    .out_15(n8_bit_enter_o_mat_2_out_15), .in_7(RID_out), .out_16(n8_bit_enter_o_mat_2_out_16),
    .in_8(RIC_out), .out_17(n8_bit_enter_o_mat_2_out_17), .in_9(and_6_out));
  Button u_RIC (.out(RIC_out));
  LED led_40 (.in(n8_bit_enter_o_mat_2_out_16));
  LED led_41 (.in(n8_bit_enter_o_mat_2_out_17));
  Button u_ISA (.out(ISA_out));
  _8_bit_enter_o_mat u_8_bit_enter_o_mat_3 (
    .out(n8_bit_enter_o_mat_1_out[23:16]), .in_1(JMP_out), .out_10(n8_bit_enter_o_mat_3_out_10),
    .in_2(HLT_out), .out_11(n8_bit_enter_o_mat_3_out_11), .in_3(COB_out),
    .out_12(n8_bit_enter_o_mat_3_out_12), .in_4(CIN_out), .out_13(n8_bit_enter_o_mat_3_out_13),
    .in_5(IST_out), .out_14(n8_bit_enter_o_mat_3_out_14), .in_6(ILD_out),
    .out_15(n8_bit_enter_o_mat_3_out_15), .in_7(ISA_out), .out_16(n8_bit_enter_o_mat_3_out_16),
    .in_8(OP2_out), .out_17(n8_bit_enter_o_mat_3_out_17), .in_9(and_6_out));
  Button OP2 (.out(OP2_out));
  LED led_42 (.in(n8_bit_enter_o_mat_3_out_16));
  LED led_43 (.in(n8_bit_enter_o_mat_3_out_17));
  Button u_STR (.out(STR_out));
  Button u_JBC (.out(JBC_out));
  _8_bit_enter_o_mat u_8_bit_enter_o_mat_4 (
    .out(n8_bit_enter_o_mat_1_out[31:24]), .in_1(NC_3_out), .out_10(n8_bit_enter_o_mat_4_out_10),
    .in_2(NC_2_out), .out_11(n8_bit_enter_o_mat_4_out_11), .in_3(OP1_out),
    .out_12(n8_bit_enter_o_mat_4_out_12), .in_4(ADA_out), .out_13(n8_bit_enter_o_mat_4_out_13),
    .in_5(ADC_out), .out_14(n8_bit_enter_o_mat_4_out_14), .in_6(IRI_out),
    .out_15(n8_bit_enter_o_mat_4_out_15), .in_7(STR_out), .out_16(n8_bit_enter_o_mat_4_out_16),
    .in_8(JBC_out), .out_17(n8_bit_enter_o_mat_4_out_17), .in_9(and_6_out));
  LED led_44 (.in(n8_bit_enter_o_mat_4_out_17));
  LED led_45 (.in(n8_bit_enter_o_mat_4_out_16));
  Button button_13 (.out(button_13_out));
  Button button_14 (.out(button_14_out));
  LED led_46 (.in(clock_2_green_out));
  DotMatrix #(.inputtype("row"), .matrixcols(8), .matrixrows(1), .dotshape("circle")) dotmatrix_2 (.row0(ram_select_o_mat_1_adress_out));
  DotMatrix #(.inputtype("row"), .matrixcols(8), .matrixrows(1), .dotshape("circle")) dotmatrix_3 (.row0(pull_resistor_3_node));
  Pull_Resistor pull_resistor_3 (.node(pull_resistor_3_node));
  assign pull_resistor_3_node = not_2_out ? ram_1_data : 8'bz;  // Controlled_Buffer controlled_buffer_1
  assign pull_resistor_3_node = ram_select_o_mat_1_write_out ? ram_select_o_mat_1_data_out : 8'bz;  // Controlled_Buffer controlled_buffer_2
  not not_2 (not_2_out, ram_select_o_mat_1_write_out);
  not not_3 (not_3_out, not_2_out);
  ROM rom_2 (.addr(ram_select_o_mat_1_rom_adress), .data(rom_2_data), .sel(1'b1));
  _8_bit_enter_o_mat u_8_bit_enter_o_mat_5 (
    .out(n8_bit_enter_o_mat_5_out), .in_1(button_1_out), .out_10(n8_bit_enter_o_mat_5_out_10),
    .in_2(button_5_out), .out_11(n8_bit_enter_o_mat_5_out_11), .in_3(button_7_out),
    .out_12(n8_bit_enter_o_mat_5_out_12), .in_4(button_8_out), .out_13(n8_bit_enter_o_mat_5_out_13),
    .in_5(button_6_out), .out_14(n8_bit_enter_o_mat_5_out_14), .in_6(button_15_out),
    .out_15(n8_bit_enter_o_mat_5_out_15), .in_7(button_17_out), .out_16(n8_bit_enter_o_mat_5_out_16),
    .in_8(button_16_out), .out_17(n8_bit_enter_o_mat_5_out_17));  // open: in_9
  Button button_15 (.out(button_15_out));
  Button button_16 (.out(button_16_out));
  Button button_17 (.out(button_17_out));
  LED led_47 (.in(n8_bit_enter_o_mat_5_out_15));
  LED led_48 (.in(n8_bit_enter_o_mat_5_out_17));
  LED led_49 (.in(n8_bit_enter_o_mat_5_out_16));
  Button button_18 (.out(button_18_out));
  Button button_19 (.out(button_19_out));
  Button button_20 (.out(button_20_out));
  _8_bit_enter_o_mat u_8_bit_enter_o_mat_6 (
    .out(n8_bit_enter_o_mat_6_out), .in_1(button_2_out), .out_10(n8_bit_enter_o_mat_6_out_10),
    .in_2(button_10_out), .out_11(n8_bit_enter_o_mat_6_out_11), .in_3(button_9_out),
    .out_12(n8_bit_enter_o_mat_6_out_12), .in_4(button_11_out), .out_13(n8_bit_enter_o_mat_6_out_13),
    .in_5(button_12_out), .out_14(n8_bit_enter_o_mat_6_out_14), .in_6(button_18_out),
    .out_15(n8_bit_enter_o_mat_6_out_15), .in_7(button_19_out), .out_16(n8_bit_enter_o_mat_6_out_16),
    .in_8(button_20_out), .out_17(n8_bit_enter_o_mat_6_out_17));  // open: in_9
  LED led_50 (.in(n8_bit_enter_o_mat_6_out_15));
  LED led_51 (.in(n8_bit_enter_o_mat_6_out_16));
  LED led_52 (.in(n8_bit_enter_o_mat_6_out_17));
  and and_4 (and_4_out, STR, and_5_out, ~clock_2_clock_out);  // AND_Gate
  and and_5 (and_5_out, STR, or_7_out);
  Adder #(.width(3)) adder_1 (
    .a(counter_1_q), .b(3'b101), .out({adder_1_out[2], adder_1_out_2[1:0]}), .cin(1'b0), .cout(adder_1_cout));
  or or_2 (ISA, rom_1_data[17], and_2_out);
  or or_3 (ILD, IRI, rom_1_data[18]);
  or or_4 (CIN, rom_1_data[20], IRI);
  or or_5 (COB, rom_1_data[21], and_2_out);
  // Probe on {register_2_q, adder_1_out_2[7:2]}
  Pull_Resistor #(.pull(1)) pull_resistor_4 (.node(pull_resistor_4_node));
  and and_6 (and_6_out, ~pull_resistor_4_node, not_4_out);  // AND_Gate
  Button RESET (.out(RESET_out));
  Button button_21 (.out(button_21_out));
  clock clock_2 (
    .HALT(HLT), .RESET(pull_resistor_5_node), .CLOCK_out(clock_2_clock_out), .button(button_14_out),
    .auto(button_13_out), .green_out(clock_2_green_out), .manual(button_21_out), .red_out(clock_2_red_out),
    .OSC(clock_1_out));
  LED led_53 (.in(clock_2_red_out));
  LED led_54 (.in(clock_2_clock_out));
  Pull_Resistor pull_resistor_5 (.node(pull_resistor_5_node));
  or or_6 (or_6_out, clock_2_clock_out, ram_select_o_mat_1_load_clock);
  DotMatrix #(.inputtype("row"), .matrixcols(8), .matrixrows(1), .dotshape("circle")) dotmatrix_4 (.row0({register_2_q, adder_1_out_2[7:2]}));
  or or_7 (or_7_out, and_5_out, clock_2_clock_out);
  buf buffer_1 (HLT, rom_1_data[22]);
  Pull_Resistor pull_resistor_6 (.node(and_6_out));
  Pull_Resistor #(.pull(1)) pull_resistor_7 (.node(pull_resistor_7_node));
  or or_8 (pull_resistor_4_node, and_6_out, pull_resistor_7_node);
  // AND_Gate and_7 has open pins: in0=pull_resistor_4_node, in1=not_4_out, out=open
  DotMatrix #(.inputtype("row"), .matrixcols(8), .matrixrows(1), .dotshape("circle")) dotmatrix_5 (.row0(controlled_buffer_3_out));
  buf buffer_2 (pull_resistor_5_node, RESET_out);
  DotMatrix #(.inputtype("row"), .matrixcols(8), .matrixrows(1), .dotshape("circle")) dotmatrix_6 (.row0(counter_2_q));
  Register register_1 (
    .D(controlled_buffer_3_out), .en(ISA), .Q(register_1_q), .clk(clock_2_clock_out),
    .clr(pull_resistor_5_node));
  RAM #(.bus("separate")) ram_1 (
    .addr(ram_select_o_mat_1_adress_out), .din(pull_resistor_3_node), .data(ram_1_data), .str(not_3_out),
    .sel(1'b1), .clk(or_6_out), .ld(1'b1));  // open: clr
  assign controlled_buffer_3_out = ILD ? ram_1_data : 8'bz;  // Controlled_Buffer controlled_buffer_3
  Register register_2 (
    .D(controlled_buffer_3_out), .en(IRI), .Q({register_2_q, adder_1_out_2[7:2]}), .clk(clock_2_clock_out),
    .clr(pull_resistor_5_node));
  assign controlled_buffer_3_out = alu_1_out;  // Buffer buffer_3, 8 bits wide
  assign controlled_buffer_3_out = ROD ? buffer_7_out : 8'bz;  // Controlled_Buffer controlled_buffer_4
  not not_4 (not_4_out, clock_2_clock_out);
  Pull_Resistor pull_resistor_8 (.node(controlled_buffer_3_out));
  assign controlled_buffer_3_out = COB ? counter_2_q : 8'bz;  // Controlled_Buffer controlled_buffer_5
  or or_9 (or_9_out, JMP, and_8_out);
  Counter counter_2 (
    .load(or_9_out), .D(controlled_buffer_3_out), .count(CIN), .Q(counter_2_q), .clk(clock_2_clock_out),
    .clr(pull_resistor_5_node));  // open: carry
  and and_8 (and_8_out, JBC, xor_1_out);
  LED led_55 (.in(xor_1_out));
  DotMatrix #(.inputtype("row"), .matrixcols(8), .matrixrows(1), .dotshape("circle")) dotmatrix_7 (.row0(register_3_q));
  assign controlled_buffer_3_out = ROA ? register_3_q : 8'bz;  // Controlled_Buffer controlled_buffer_6
  Register register_3 (
    .D(controlled_buffer_3_out), .en(RIA), .Q(register_3_q), .clk(clock_2_clock_out),
    .clr(pull_resistor_5_node));
  DotMatrix #(.inputtype("row"), .matrixcols(8), .matrixrows(1), .dotshape("circle")) dotmatrix_8 (.row0(register_4_q));
  assign controlled_buffer_3_out = ROB ? register_4_q : 8'bz;  // Controlled_Buffer controlled_buffer_7
  Register register_4 (
    .D(controlled_buffer_3_out), .en(RIB), .Q(register_4_q), .clk(clock_2_clock_out), .clr(or_10_out));
  ALU alu_1 (
    .OUT(alu_1_out), .A(register_3_q), .B(register_4_q), .Cin(ACR), .inv_A(AIA),
    .inv_B___shit_direction(AIB), .disable_AND___rotate(ADA), .inv_OUT(AIO), .disable_carry(ADC),
    .enable_out(ALO), .shift_mode(OPTN0), .flags(alu_1_flags));  // open: Cout
  DotMatrix #(.inputtype("row"), .matrixcols(2), .matrixrows(1), .dotshape("circle")) dotmatrix_9 (.row0(register_5_q));
  Register #(.width(2)) register_5 (
    .D(alu_1_flags), .en(FRI), .Q(register_5_q), .clk(clock_2_clock_out), .clr(pull_resistor_5_node));
  nor nor_2 (nor_2_out, register_5_q[1], register_5_q[0]);
  DotMatrix #(.inputtype("row"), .matrixcols(8), .matrixrows(1), .dotshape("circle")) dotmatrix_10 (.row0(register_6_q));
  assign controlled_buffer_3_out = ROC ? register_6_q : 8'bz;  // Controlled_Buffer controlled_buffer_8
  Register register_6 (
    .D(controlled_buffer_3_out), .en(RIC), .Q(register_6_q), .clk(clock_2_clock_out),
    .clr(pull_resistor_5_node));
  Button RESET_2 (.out(RESET_2_out));
  xor xor_1 (xor_1_out, OPTN2, FRBC);
  or or_10 (or_10_out, RSTB, pull_resistor_5_node);
  and and_9 (and_9_out, register_5_q[0], ~register_5_q[1]);  // AND_Gate
  // Probe on register_6_q
  // Probe on register_6_q
  Multiplexer #(.select(2), .enable("false")) multiplexer_1 (
    .in0(register_5_q[1]), .in1(and_9_out), .in2(nor_2_out), .in3(register_5_q[0]), .out(FRBC),
    .sel({OPTN1, OPTN0}));
  buf buffer_4 (buffer_4_out, pull_resistor_5_node);
  buf buffer_5 (buffer_5_out, clock_2_clock_out);
  buf buffer_6 (buffer_6_out, RID);
  assign buffer_7_out = or_19_out;  // Buffer buffer_7, 8 bits wide
  assign {buffer_8_out_2[7], buffer_8_out} = controlled_buffer_3_out;  // Buffer buffer_8, 8 bits wide
  buf buffer_9 (buffer_9_out, ROD);
  Counter #(.width(4), .max('hf)) counter_3 (
    .load(1'b0), .count(1'b1), .Q(counter_3_q), .clk(undriven), .clr(or_11_out));  // open: D, carry
  or or_11 (or_11_out, RESET_2_out, and_10_out);
  and and_10 (and_10_out, ~undriven, comparator_1_eq);  // AND_Gate
  Pull_Resistor pull_resistor_9 (.node(pull_resistor_9_node));
  // Probe on or_19_out
  and and_11 (HLT, ~or_22_out, buffer_9_out);  // AND_Gate
  Comparator #(.width(4)) comparator_1 (.a(4'b0100), .b(counter_3_q), .eq(comparator_1_eq));  // open: gt, lt
  Transistor #(.\type ("n"), .width(32)) transistor_1 (
    .in(register_7_q), .out(pull_resistor_9_node), .gate(adder_1_cout));
  xor xor_2 (xor_2_out, 1'b0, 1'b0);
  not not_5 (not_5_out, 1'b0);
  nand nand_1 (nand_1_out, not_5_out, 1'b0);
  nand nand_2 (nand_2_out, 1'b0, 1'b0);
  nand nand_3 (nand_3_out, not_5_out, 1'b0);
  nand nand_4 (nand_4_out, 1'b0, 1'b0);
  Decoder #(.select(4), .enable("false")) decoder_1 (
    .out0(decoder_1_out0), .out1(decoder_1_out1), .out2(decoder_1_out2), .out3(decoder_1_out3),
    .sel(counter_3_q));  // open: out4, out5, out6, out7, out8, out9, out10, out11, out12, out13, out14, out15
  nor nor_3 (nor_3_out, xor_2_out, not_6_out);
  not not_6 (not_6_out, 1'b0);
  not not_7 (not_7_out, 1'b0);
  nand nand_5 (nand_5_out, nand_1_out, nand_2_out);
  nand nand_6 (nand_6_out, nand_3_out, nand_4_out);
  ROM #(.addrWidth(12)) rom_3 (.addr({counter_3_q, adder_1_out_2}), .data(rom_3_data), .sel(1'b1));
  LED led_56 (.in(not_8_out));
  not not_8 (not_8_out, nor_4_out);
  nor nor_4 (nor_4_out, nor_3_out, 1'b0);
  nand nand_7 (nand_7_out, nand_5_out, not_7_out);
  nand nand_8 (nand_8_out, nand_7_out, nand_9_out);
  LED led_57 (.in(nand_8_out));
  nand nand_9 (nand_9_out, 1'b0, nand_6_out);
  Register register_7 (.D(rom_3_data), .en(decoder_1_out0), .Q(register_7_q[7:0]), .clk(undriven), .clr(RESET_2_out));
  // Probe on register_7_q[7:0]
  // Probe on register_7_q[15:8]
  Register register_8 (.D(rom_3_data), .en(decoder_1_out1), .Q(register_7_q[15:8]), .clk(undriven), .clr(RESET_2_out));
  Register register_9 (.D(rom_3_data), .en(decoder_1_out2), .Q(register_7_q[23:16]), .clk(undriven), .clr(RESET_2_out));
  // Probe on register_7_q[23:16]
  // Probe on register_7_q[31:24]
  Register register_10 (
    .D(rom_3_data), .en(decoder_1_out3), .Q(register_7_q[31:24]), .clk(undriven), .clr(RESET_2_out));
  TTY tty_1 (.data(buffer_8_out), .clk(buffer_5_out), .we(buffer_6_out), .clr(buffer_4_out));
  Button button_22 (.out(button_22_out));
  Button button_23 (.out(button_23_out));
  Button button_24 (.out(button_24_out));
  Button button_25 (.out(button_25_out));
  Button button_26 (.out(button_26_out));
  Button button_27 (.out(button_27_out));
  or or_12 (or_12_out, button_27_out, button_26_out, button_25_out);
  or or_13 (or_13_out, button_24_out, button_23_out, button_22_out);
  Button button_28 (.out(button_28_out));
  Button button_29 (.out(button_29_out));
  Button button_30 (.out(button_30_out));
  or or_14 (or_14_out, button_30_out, button_29_out, button_28_out);
  or or_15 (or_15_out, button_22_out, button_25_out, button_28_out);
  or or_16 (or_16_out, button_23_out, button_26_out, button_29_out);
  or or_17 (or_17_out, button_24_out, button_27_out, button_30_out);
  or or_18 (or_19_out[1], or_17_out, or_16_out);
  or or_19 (or_19_out[0], or_17_out, or_15_out);
  or or_20 (or_19_out[2], or_14_out, or_13_out);
  or or_21 (or_19_out[3], or_14_out, or_12_out);
  Button button_31 (.out(or_19_out[7]));
  Pull_Resistor pull_resistor_10 (.node(or_19_out));
  or or_22 (or_22_out, or_19_out[0], or_19_out[1], or_19_out[7], or_19_out[2], or_19_out[3]);

  // Notes on the sheet:
  //   press to load
  //   this is funtionally equal to GR8CPU, this is NOT logically equal to GR8CPU
  //   program this ROM
  //   adress
  //   data
  //   contents of rom_1 (hex, n*v repeats v):
  //   2000000 0 0 0 160000 2040040 0 0 2140040 0 0 0 2000500 0 0 0 2000600 0 0 0 2001040 0 0 0 2002040 0 0
  //   0 160000 40080 2004060 0 160000 40080 2004068 0 140080 2004060 0 0 140080 2004068 0 0 160000 40080
  //   200406a 0 160000 40080 2004062 0 140080 200406a 0 0 140080 2004062 0 0 160000 40080 200400a 0 140080
  //   200400a 0 0 2840000 0 0 0 100000 3040000 0 0 100000 3050000 0 0 100000 3040010 0 0 100000 3050010 0
  //   0 100000 23040000 0 0 100000 23050000 0 0 100000 23040010 0 0 100000 23050010 0 0 160000 40080
  //   1a004060 0 140080 1a004060 0 0 160000 40080 1a004067 0 140080 1a004067 0 0 160000 40080 a004060 0
  //   140080 a004060 0 0 2004070 0 0 0 2004072 0 0 0 160000 2080400 0 0 80160000 40040 84028 2040040
  //   80000000 2004068 0 0 80160000 40040 84022 2040040 80000000 2004062 0 0 160000 40040 84030 2040040
  //   160000 40040 84032 2040040 140080 20020 2040040 0 12004070 0 0 0 12004072 0 0 0 160000 40040
  //   10084030 2040040 160000 40040 10084032 2040040 80001040 2004168 0 0 80001040 2004162 0 0 1040
  //   2004170 0 0 1040 2004172 0 0 1040 12004170 0 0 1040 12004172 46*0 400000 2000000
  //   contents of rom_2 (hex, n*v repeats v):
  //   11 f4 54 69 65 a 0 20 77 69 6e 73 a 1 20 30 78 2d 2b 2d 2b 2d a 8*0 2 27 22 ee 2 0 22 1d 1 1d 29 17
  //   22 1b 2 3 22 1c 11 36 2 7c 4 28 1b 28 1b 1d 3 29 e 4 25 1c 13 33 2 a 4 23 1d 10 3 2 11 22 e9 13 e8 2
  //   0 22 1b 2 ff 22 1d 1 d 10 1 2 54 12 61 20 22 1e 1 1b 29 17 f 1e 12 dc 1c 1d 22 1d 23 1b 10 3 13 63 1
  //   1d 10 0 13 dc 1 18 1d 30 1c 1e 12 95 1 17 4*2b 1c 19 1c 1e 13 dc 23 1a 10 9 17 e0 25 d 1f 1 24 22 d
  //   1 d 29 e 4 22 6 2 a 4 6 22 1b 1d 3 26 22 1c 28 1b 28 1b 1 d 22 1e 1 1c 29 17 22 1d 28 1d 28 1d 27 1e
  //   27 1e 25 1b 13 bc 1 1d 1d 3 13 a6 1 1c 9 17 22 d9 29 0 1a 1e 22 0 11 1f 2 6 11 e2 2 2 22 e9 2 f3 22
  //   ee 1 0 4 10 a 12 0 23 e9 11 e8 6 2 0 22 17 22 18 22 19 22 1a 11 1f
  //   buffer_1 drives only 1 and floats otherwise
  //   data out
  //   RESET
  //   clock
  //   write
  //   data in
  //   read
  //   0: Cout, 1: Zero
  //   and_11 drives only 1 and floats otherwise
  //   contents of rom_3 (hex, n*v repeats v):
  //   5*0 40 0 0 40 11*0 40 0 0 0 40 4*0 80 60 0 0 80 68 0 80 60 0 0 80 68 0 0 0 80 6a 0 0 80 62 0 80 6a 0
  //   0 80 62 0 0 0 80 a 0 80 a 15*0 10 0 0 0 10 11*0 10 0 0 0 10 0 0 0 80 60 0 80 60 0 0 0 80 67 0 80 67
  //   0 0 0 80 60 0 80 60 0 0 70 0 0 0 72 8*0 40 28 40 0 68 0 0 0 40 22 40 0 62 0 0 0 40 30 40 0 40 32 40
  //   80 20 40 0 70 0 0 0 72 4*0 40 30 40 0 40 32 40 40 68 0 0 40 62 0 0 40 70 0 0 40 72 0 0 40 70 0 0 40
  //   72 62*0 5 0 0 0 6 0 0 0 10 0 0 0 20 5*0 40 0 0 0 40 0 0 40 0 0 0 40 4*0 40 0 0 0 40 0 0 40 0 0 0 40
  //   4*0 40 0 0 40 40*0 40 0 0 40 4*0 40 0 0 40 4*0 40 0 0 40 0 0 40 0 0 0 40 4*0 4 4*0 40 0 0 40 4*0 40
  //   0 0 40 4*0 40 0 0 0 40 5*0 40 0 0 0 40 5*0 40 0 0 0 40 0 10 41 0 0 10 41 0 0 10 41 0 0 10 41 0 0 10
  //   41 0 0 10 41 54*0 16 4 0 0 14 19*0 16 4 0 0 16 4 0 0 14 0 0 0 14 0 0 0 16 4 0 0 16 4 0 0 14 0 0 0 14
  //   0 0 0 16 4 0 0 14 0 0 0 84 0 0 0 10 4 0 0 10 5 0 0 10 4 0 0 10 5 0 0 10 4 0 0 10 5 0 0 10 4 0 0 10 5
  //   0 0 16 4 0 0 14 0 0 0 16 4 0 0 14 0 0 0 16 4 0 0 14 11*0 16 8 0 0 16 4 8 4 4*0 16 4 8 4 4*0 16 4 8 4
  //   16 4 8 4 14 2 4 9*0 16 4 8 4 16 4 8 4 68*0 40 0 0 0 2 4*0 2 0 0 2 0 0 0 2 0 0 0 2 0 0 0 2 0 0 0 2
  //   5*0 2 0 0 0 2 0 0 2 0 0 0 2 4*0 2 0 0 0 2 0 0 2 0 0 0 2 4*0 2 0 0 2 0 0 2 4*0 3 0 0 0 3 0 0 0 3 0 0
  //   0 3 0 0 0 23 0 0 0 23 0 0 0 23 0 0 0 23 4*0 1a 0 0 1a 4*0 1a 0 0 1a 4*0 a 0 0 a 0 0 2 0 0 0 2 4*0 2
  //   0 0 80 0 0 2 80 2 0 0 80 0 0 2 80 2 5*0 2 0 0 0 2 0 0 2 0 12 0 0 0 12 5*0 10 2 0 0 10 2 80 2 0 0 80
  //   2 0 0 0 2 0 0 0 2 0 0 0 12 0 0 0 12 47*0 2
endmodule

module clock (
  input  button,
  input  auto,
  input  manual,
  input  RESET,
  input  HALT,
  input  OSC,
  output green_out,
  output red_out,
  output CLOCK_out
);

  wire and_1_out, and_2_out, not_1_out, not_2_out, or_1_out, s_r_ff_2_q;

  not not_1 (not_1_out, HALT);
  not not_2 (not_2_out, OSC);
  and and_1 (and_1_out, not_2_out, not_1_out);
  and and_2 (and_2_out, OSC, not_1_out);
  S_R_Flip_Flop s_r_ff_1 (.Q(green_out), .Qn(red_out), .preset(auto), .reset(or_1_out));  // open: S, clk, R, en
  or or_1 (or_1_out, manual, RESET);
  S_R_Flip_Flop s_r_ff_2 (.Q(s_r_ff_2_q), .preset(and_2_out), .reset(and_1_out));  // open: S, clk, R, Qn, en
  Multiplexer #(.enable("false")) multiplexer_1 (.in0(s_r_ff_2_q), .in1(button), .out(CLOCK_out), .sel(red_out));
endmodule

module _7_segment_number_display (
  input  [1:0] MODE,
  input  [7:0] DATA,
  output out_3,
  output out_4,
  output out_5,
  output out_6,
  output out_7,
  output out_8,
  output out_9,
  output out_10,
  output out_11,
  output out_12,
  output out_13,
  output out_14,
  output out_15,
  output out_16,
  output out_17,
  output out_18,
  output out_19,
  output out_20,
  output out_21,
  output out_22,
  output out_23,
  output out_24,
  output out_25,
  output out_26,
  output out_27,
  output out_28,
  output out_29,
  output out_30,
  output out_31,
  output out_32,
  output out_33,
  output out_34
);

  wire clock_1_out, decoder_1_out0, decoder_1_out1, decoder_1_out2, decoder_1_out3;
  wire [1:0] counter_1_q;
  wire [7:0] rom_1_data;

  Pull_Resistor pull_resistor_1 (.node(MODE));
  Pull_Resistor pull_resistor_2 (.node(DATA));
  Clock clock_1 (.out(clock_1_out));
  Counter #(.width(2), .max('h3)) counter_1 (
    .count(1'b1), .Q(counter_1_q), .clk(clock_1_out));  // open: load, D, carry, clr
  ROM #(.addrWidth(12)) rom_1 (.addr({counter_1_q, MODE, DATA}), .data(rom_1_data), .sel(1'b1));
  Decoder #(.select(2), .disabled(0), .enable("false")) decoder_1 (
    .out0(decoder_1_out0), .out1(decoder_1_out1), .out2(decoder_1_out2), .out3(decoder_1_out3),
    .sel(counter_1_q));
  Register #(.trigger("falling")) register_1 (
    .D(rom_1_data), .en(1'b1), .Q({out_22, out_3, out_4, out_19, out_20, out_21, out_6, out_5}),
    .clk(decoder_1_out3));  // open: clr
  Register #(.trigger("falling")) register_2 (
    .D(rom_1_data), .en(1'b1), .Q({out_26, out_7, out_8, out_23, out_24, out_25, out_10, out_9}),
    .clk(decoder_1_out2));  // open: clr
  Register #(.trigger("falling")) register_3 (
    .D(rom_1_data), .en(1'b1), .Q({out_30, out_11, out_12, out_27, out_28, out_29, out_14, out_13}),
    .clk(decoder_1_out1));  // open: clr
  Register #(.trigger("falling")) register_4 (
    .D(rom_1_data), .en(1'b1), .Q({out_34, out_15, out_16, out_31, out_32, out_33, out_18, out_17}),
    .clk(decoder_1_out0));  // open: clr

  // Notes on the sheet:
  //   contents of rom_1 (hex, n*v repeats v):
  //   3f 6 5b 4f 66 6d 7d 7 7f 6f 3f 6 5b 4f 66 6d 7d 7 7f 6f 3f 6 5b 4f 66 6d 7d 7 7f 6f 3f 6 5b 4f 66 6d
  //   7d 7 7f 6f 3f 6 5b 4f 66 6d 7d 7 7f 6f 3f 6 5b 4f 66 6d 7d 7 7f 6f 3f 6 5b 4f 66 6d 7d 7 7f 6f 3f 6
  //   5b 4f 66 6d 7d 7 7f 6f 3f 6 5b 4f 66 6d 7d 7 7f 6f 3f 6 5b 4f 66 6d 7d 7 7f 6f 3f 6 5b 4f 66 6d 7d 7
  //   7f 6f 3f 6 5b 4f 66 6d 7d 7 7f 6f 3f 6 5b 4f 66 6d 7d 7 7f 6f 3f 6 5b 4f 66 6d 7d 7 7f 6f 3f 6 5b 4f
  //   66 6d 7d 7 7f 6f 3f 6 5b 4f 66 6d 7d 7 7f 6f 3f 6 5b 4f 66 6d 7d 7 7f 6f 3f 6 5b 4f 66 6d 7d 7 7f 6f
  //   3f 6 5b 4f 66 6d 7d 7 7f 6f 3f 6 5b 4f 66 6d 7d 7 7f 6f 3f 6 5b 4f 66 6d 7d 7 7f 6f 3f 6 5b 4f 66 6d
  //   7d 7 7f 6f 3f 6 5b 4f 66 6d 7d 7 7f 6f 3f 6 5b 4f 66 6d 7d 7 7f 6f 3f 6 5b 4f 66 6d 7d 7 7f 6f 3f 6
  //   5b 4f 66 6d 3f 6 5b 4f 66 6d 7d 7 7f 6f 3f 6 5b 4f 66 6d 7d 7 7f 6f 3f 6 5b 4f 66 6d 7d 7 7f 6f 3f 6
  //   5b 4f 66 6d 7d 7 7f 6f 3f 6 5b 4f 66 6d 7d 7 7f 6f 3f 6 5b 4f 66 6d 7d 7 7f 6f 3f 6 5b 4f 66 6d 7d 7
  //   7f 6f 3f 6 5b 4f 66 6d 7d 7 7f 6f 3f 6 5b 4f 66 6d 7d 7 7f 6f 3f 6 5b 4f 66 6d 7d 7 7f 6f 3f 6 5b 4f
  //   66 6d 7d 7 7f 6f 3f 6 5b 4f 66 6d 7d 7 7f 6f 3f 6 5b 4f 66 6d 7d 7 7f 7 7d 6d 66 4f 5b 6 3f 6f 7f 7
  //   7d 6d 66 4f 5b 6 3f 6f 7f 7 7d 6d 66 4f 5b 6 3f 6f 7f 7 7d 6d 66 4f 5b 6 3f 6f 7f 7 7d 6d 66 4f 5b 6
  //   3f 6f 7f 7 7d 6d 66 4f 5b 6 3f 6f 7f 7 7d 6d 66 4f 5b 6 3f 6f 7f 7 7d 6d 66 4f 5b 6 3f 6f 7f 7 7d 6d
  //   66 4f 5b 6 3f 6f 7f 7 7d 6d 66 4f 5b 6 3f 6f 7f 7 7d 6d 66 4f 5b 6 3f 6f 7f 7 7d 6d 66 4f 5b 6 3f 6f
  //   7f 7 7d 6d 66 4f 5b 6 3f 6 5b 4f 66 6d 7d 7 7f 6f 77 7c 39 5e 79 71 3f 6 5b 4f 66 6d 7d 7 7f 6f 77
  //   7c 39 5e 79 71 3f 6 5b 4f 66 6d 7d 7 7f 6f 77 7c 39 5e 79 71 3f 6 5b 4f 66 6d 7d 7 7f 6f 77 7c 39 5e
  //   79 71 3f 6 5b 4f 66 6d 7d 7 7f 6f 77 7c 39 5e 79 71 3f 6 5b 4f 66 6d 7d 7 7f 6f 77 7c 39 5e 79 71 3f
  //   6 5b 4f 66 6d 7d 7 7f 6f 77 7c 39 5e 79 71 3f 6 5b 4f 66 6d 7d 7 7f 6f 77 7c 39 5e 79 71 3f 6 5b 4f
  //   66 6d 7d 7 7f 6f 77 7c 39 5e 79 71 3f 6 5b 4f 66 6d 7d 7 7f 6f 77 7c 39 5e 79 71 3f 6 5b 4f 66 6d 7d
  //   7 7f 6f 77 7c 39 5e 79 71 3f 6 5b 4f 66 6d 7d 7 7f 6f 77 7c 39 5e 79 71 3f 6 5b 4f 66 6d 7d 7 7f 6f
  //   77 7c 39 5e 79 71 3f 6 5b 4f 66 6d 7d 7 7f 6f 77 7c 39 5e 79 71 3f 6 5b 4f 66 6d 7d 7 7f 6f 77 7c 39
  //   5e 79 71 3f 6 5b 4f 66 6d 7d 7 7f 6f 77 7c 39 5e 79 71 266*0 10*6 10*5b 10*4f 10*66 10*6d 10*7d 10*7
  //   10*7f 10*6f 10*3f 10*6 10*5b 10*4f 10*66 10*6d 10*7d 10*7 10*7f 10*6f 10*3f 10*6 10*5b 10*4f 10*66
  //   6*6d 10*0 10*6 10*5b 10*4f 10*66 10*6d 10*7d 10*7 10*7f 10*6f 10*3f 10*6 17*5b 10*6 10*3f 10*6f
  //   10*7f 10*7 10*7d 10*6d 10*66 10*4f 10*5b 10*6 9*40 16*3f 16*6 16*5b 16*4f 16*66 16*6d 16*7d 16*7
  //   16*7f 16*6f 16*77 16*7c 16*39 16*5e 16*79 16*71 356*0 100*6 56*5b 100*0 57*6 90*40 905*0 29*40
endmodule

module ALU (
  input  [7:0] A,
  input  [7:0] B,
  input  Cin,
  input  inv_A,
  input  inv_B___shit_direction,
  input  disable_AND___rotate,
  input  inv_OUT,
  input  disable_carry,
  input  enable_out,
  input  shift_mode,
  output [7:0] OUT,
  output Cout,
  output [1:0] flags
);

  wire and_1_out, and_2_out, and_3_out, and_4_out, and_5_out, and_6_out, and_7_out, and_8_out, and_9_out,
       and_10_out, and_11_out, and_12_out, and_13_out, and_14_out, and_15_out, and_16_out, and_17_out,
       and_18_out, and_19_out, and_20_out, and_21_out, and_22_out, and_23_out, and_24_out, and_25_out,
       and_26_out, and_27_out, and_28_out, and_29_out, and_30_out, and_31_out, and_32_out, and_33_out,
       and_34_out, and_35_out, and_36_out, and_37_out, and_38_out, and_39_out, and_40_out, and_41_out,
       and_42_out, and_43_out, and_44_out, and_45_out, and_46_out, and_47_out, and_48_out, and_49_out,
       and_50_out, and_51_out, and_52_out, and_53_out, and_54_out, and_55_out, and_56_out, and_57_out,
       and_58_out, and_59_out, and_60_out, and_61_out, and_62_out, and_63_out, and_64_out, and_65_out,
       and_66_out, and_67_out, and_68_out, and_69_out, and_70_out, and_71_out, and_72_out, and_73_out,
       and_74_out, and_75_out, and_76_out, and_77_out, and_78_out, and_79_out, and_80_out, and_81_out,
       and_83_out, and_84_out, and_85_out, and_86_out, and_87_out, and_88_out, and_89_out, and_90_out,
       and_91_out, controlled_buffer_22_out, nor_2_out, nor_3_out, nor_4_out, nor_5_out, nor_6_out,
       nor_7_out, nor_8_out, nor_9_out, not_1_out, not_2_out, not_3_out, not_4_out, not_5_out, not_6_out,
       not_7_out, not_8_out, not_9_out, not_10_out, not_11_out, or_1_out, or_2_out, or_3_out, or_4_out,
       or_5_out, or_6_out, or_7_out, or_8_out, or_9_out, or_10_out, or_11_out, or_12_out, or_13_out,
       or_14_out, or_15_out, or_16_out, or_17_out, or_18_out, or_19_out, or_20_out, or_21_out, or_22_out,
       or_23_out, or_24_out, or_25_out, or_26_out, or_27_out, or_28_out, or_29_out, or_30_out, or_31_out,
       or_32_out, or_33_out, or_34_out, or_35_out, or_36_out, or_37_out, or_38_out, or_39_out, or_40_out,
       pull_resistor_1_node, pull_resistor_3_node, xor_1_out, xor_2_out, xor_3_out, xor_4_out, xor_5_out,
       xor_6_out, xor_7_out, xor_8_out, xor_9_out, xor_10_out, xor_11_out, xor_12_out, xor_13_out,
       xor_14_out, xor_15_out, xor_16_out, xor_25_out, xor_26_out, xor_27_out, xor_28_out, xor_29_out,
       xor_30_out, xor_31_out, xor_32_out, xor_33_out, xor_34_out, xor_35_out, xor_36_out, xor_37_out,
       xor_38_out, xor_39_out, xor_40_out;
  wire [7:0] controlled_buffer_4_out, controlled_buffer_6_out, xor_17_out;

  assign OUT = enable_out ? controlled_buffer_4_out : 8'bz;  // Controlled_Buffer controlled_buffer_1
  and and_1 (and_1_out, xor_1_out, xor_2_out);
  xor xor_1 (xor_1_out, B[0], inv_B___shit_direction);
  xor xor_2 (xor_2_out, A[0], inv_A);
  or or_1 (or_1_out, xor_1_out, xor_2_out);
  and and_2 (and_2_out, xor_3_out, xor_4_out);
  xor xor_3 (xor_3_out, B[1], inv_B___shit_direction);
  or or_2 (or_2_out, xor_3_out, xor_4_out);
  xor xor_4 (xor_4_out, A[1], inv_A);
  and and_3 (and_3_out, xor_5_out, xor_6_out);
  xor xor_5 (xor_5_out, B[2], inv_B___shit_direction);
  xor xor_6 (xor_6_out, A[2], inv_A);
  or or_3 (or_3_out, xor_5_out, xor_6_out);
  xor xor_7 (xor_7_out, B[3], inv_B___shit_direction);
  and and_4 (and_4_out, xor_7_out, xor_8_out);
  xor xor_8 (xor_8_out, A[3], inv_A);
  or or_4 (or_4_out, xor_7_out, xor_8_out);
  xor xor_9 (xor_9_out, B[4], inv_B___shit_direction);
  and and_5 (and_5_out, xor_9_out, xor_10_out);
  xor xor_10 (xor_10_out, A[4], inv_A);
  or or_5 (or_5_out, xor_9_out, xor_10_out);
  and and_6 (and_6_out, xor_11_out, xor_12_out);
  xor xor_11 (xor_11_out, B[5], inv_B___shit_direction);
  or or_6 (or_6_out, xor_11_out, xor_12_out);
  xor xor_12 (xor_12_out, A[5], inv_A);
  xor xor_13 (xor_13_out, B[6], inv_B___shit_direction);
  and and_7 (and_7_out, xor_13_out, xor_14_out);
  or or_7 (or_7_out, xor_13_out, xor_14_out);
  xor xor_14 (xor_14_out, A[6], inv_A);
  and and_8 (and_8_out, xor_15_out, xor_16_out);
  xor xor_15 (xor_15_out, B[7], inv_B___shit_direction);
  or or_8 (or_8_out, xor_15_out, xor_16_out);
  xor xor_16 (xor_16_out, A[7], inv_A);
  and and_9 (and_9_out, ~disable_AND___rotate, and_1_out);  // AND_Gate
  and and_10 (and_10_out, ~disable_AND___rotate, and_2_out);  // AND_Gate
  and and_11 (and_11_out, ~disable_AND___rotate, and_3_out);  // AND_Gate
  and and_12 (and_12_out, ~disable_AND___rotate, and_4_out);  // AND_Gate
  and and_13 (and_13_out, ~disable_AND___rotate, and_5_out);  // AND_Gate
  and and_14 (and_14_out, ~disable_AND___rotate, and_6_out);  // AND_Gate
  and and_15 (and_15_out, ~disable_AND___rotate, and_7_out);  // AND_Gate
  and and_16 (and_16_out, ~disable_AND___rotate, and_8_out);  // AND_Gate
  assign Cout = not_1_out ? and_41_out : 1'bz;  // Controlled_Buffer controlled_buffer_2
  and and_17 (and_17_out, Cin, ~disable_carry);  // AND_Gate
  and and_18 (and_18_out, and_17_out, and_19_out);
  and and_19 (and_19_out, ~and_9_out, or_1_out);  // AND_Gate
  or or_9 (or_9_out, and_17_out, and_19_out);
  or or_10 (or_10_out, and_1_out, and_18_out);
  and and_20 (and_20_out, or_10_out, ~disable_carry);  // AND_Gate
  and and_21 (and_21_out, and_20_out, and_22_out);
  and and_22 (and_22_out, ~and_10_out, or_2_out);  // AND_Gate
  or or_11 (or_11_out, and_20_out, and_22_out);
  or or_12 (or_12_out, and_2_out, and_21_out);
  and and_23 (and_23_out, or_12_out, ~disable_carry);  // AND_Gate
  and and_24 (and_24_out, and_23_out, and_25_out);
  and and_25 (and_25_out, ~and_11_out, or_3_out);  // AND_Gate
  or or_13 (or_13_out, and_23_out, and_25_out);
  or or_14 (or_14_out, and_3_out, and_24_out);
  and and_26 (and_26_out, or_14_out, ~disable_carry);  // AND_Gate
  and and_27 (and_27_out, and_26_out, and_28_out);
  and and_28 (and_28_out, ~and_12_out, or_4_out);  // AND_Gate
  or or_15 (or_15_out, and_26_out, and_28_out);
  or or_16 (or_16_out, and_4_out, and_27_out);
  and and_29 (and_29_out, or_16_out, ~disable_carry);  // AND_Gate
  and and_30 (and_30_out, and_29_out, and_31_out);
  and and_31 (and_31_out, ~and_13_out, or_5_out);  // AND_Gate
  or or_17 (or_17_out, and_29_out, and_31_out);
  or or_18 (or_18_out, and_5_out, and_30_out);
  and and_32 (and_32_out, or_18_out, ~disable_carry);  // AND_Gate
  and and_33 (and_33_out, and_32_out, and_34_out);
  and and_34 (and_34_out, ~and_14_out, or_6_out);  // AND_Gate
  or or_19 (or_19_out, and_32_out, and_34_out);
  or or_20 (or_20_out, and_6_out, and_33_out);
  and and_35 (and_35_out, or_20_out, ~disable_carry);  // AND_Gate
  and and_36 (and_36_out, and_35_out, and_37_out);
  and and_37 (and_37_out, ~and_15_out, or_7_out);  // AND_Gate
  or or_21 (or_21_out, and_35_out, and_37_out);
  or or_22 (or_22_out, and_7_out, and_36_out);
  and and_38 (and_38_out, or_22_out, ~disable_carry);  // AND_Gate
  and and_39 (and_39_out, and_38_out, and_40_out);
  and and_40 (and_40_out, ~and_16_out, or_8_out);  // AND_Gate
  or or_23 (or_23_out, and_38_out, and_40_out);
  or or_24 (or_24_out, and_8_out, and_39_out);
  and and_41 (and_41_out, or_24_out, ~disable_carry);  // AND_Gate
  assign Cout = shift_mode ? controlled_buffer_22_out : 1'bz;  // Controlled_Buffer controlled_buffer_3
  not not_1 (not_1_out, shift_mode);
  and and_42 (and_42_out, ~disable_AND___rotate, and_18_out);  // AND_Gate
  and and_43 (and_43_out, ~and_42_out, or_9_out);  // AND_Gate
  and and_44 (and_44_out, ~disable_AND___rotate, and_21_out);  // AND_Gate
  and and_45 (and_45_out, ~and_44_out, or_11_out);  // AND_Gate
  and and_46 (and_46_out, ~disable_AND___rotate, and_24_out);  // AND_Gate
  and and_47 (and_47_out, ~and_46_out, or_13_out);  // AND_Gate
  and and_48 (and_48_out, ~disable_AND___rotate, and_27_out);  // AND_Gate
  and and_49 (and_49_out, ~and_48_out, or_15_out);  // AND_Gate
  and and_50 (and_50_out, ~disable_AND___rotate, and_30_out);  // AND_Gate
  and and_51 (and_51_out, ~and_50_out, or_17_out);  // AND_Gate
  and and_52 (and_52_out, ~disable_AND___rotate, and_33_out);  // AND_Gate
  and and_53 (and_53_out, ~and_52_out, or_19_out);  // AND_Gate
  and and_54 (and_54_out, ~disable_AND___rotate, and_36_out);  // AND_Gate
  and and_55 (and_55_out, ~and_54_out, or_21_out);  // AND_Gate
  and and_56 (and_56_out, ~disable_AND___rotate, and_39_out);  // AND_Gate
  and and_57 (and_57_out, ~and_56_out, or_23_out);  // AND_Gate
  xor xor_17 (xor_17_out[0], inv_OUT, and_43_out);
  xor xor_18 (xor_17_out[1], inv_OUT, and_45_out);
  xor xor_19 (xor_17_out[2], inv_OUT, and_47_out);
  xor xor_20 (xor_17_out[3], inv_OUT, and_49_out);
  xor xor_21 (xor_17_out[4], inv_OUT, and_51_out);
  xor xor_22 (xor_17_out[5], inv_OUT, and_53_out);
  xor xor_23 (xor_17_out[6], inv_OUT, and_55_out);
  xor xor_24 (xor_17_out[7], inv_OUT, and_57_out);
  nor nor_1 (flags[1], controlled_buffer_4_out[7], controlled_buffer_4_out[6], controlled_buffer_4_out[5], controlled_buffer_4_out[4], controlled_buffer_4_out[3], controlled_buffer_4_out[2], controlled_buffer_4_out[1], controlled_buffer_4_out[0]);
  Pull_Resistor pull_resistor_1 (.node(pull_resistor_1_node));
  assign controlled_buffer_4_out = not_2_out ? xor_17_out : 8'bz;  // Controlled_Buffer controlled_buffer_4
  assign controlled_buffer_4_out = shift_mode ? controlled_buffer_6_out : 8'bz;  // Controlled_Buffer controlled_buffer_5
  not not_2 (not_2_out, shift_mode);
  xor xor_25 (xor_25_out, A[0], inv_A);
  xor xor_26 (xor_26_out, B[0], inv_B___shit_direction);
  xor xor_27 (xor_27_out, A[1], inv_A);
  xor xor_28 (xor_28_out, B[1], inv_B___shit_direction);
  xor xor_29 (xor_29_out, A[2], inv_A);
  xor xor_30 (xor_30_out, B[2], inv_B___shit_direction);
  xor xor_31 (xor_31_out, A[3], inv_A);
  xor xor_32 (xor_32_out, B[3], inv_B___shit_direction);
  xor xor_33 (xor_33_out, A[4], inv_A);
  xor xor_34 (xor_34_out, B[4], inv_B___shit_direction);
  xor xor_35 (xor_35_out, A[5], inv_A);
  xor xor_36 (xor_36_out, B[5], inv_B___shit_direction);
  xor xor_37 (xor_37_out, A[6], inv_A);
  xor xor_38 (xor_38_out, B[6], inv_B___shit_direction);
  ExactlyOne xor_39 (.out(xor_39_out), .in0(A[7]), .in1(pull_resistor_1_node), .in2(inv_A));
  ExactlyOne xor_40 (.out(xor_40_out), .in0(B[7]), .in1(pull_resistor_1_node), .in2(inv_B___shit_direction));
  and and_58 (and_58_out, ~xor_25_out, xor_26_out);  // AND_Gate
  and and_59 (and_59_out, xor_25_out, ~xor_26_out);  // AND_Gate
  and and_60 (and_60_out, ~xor_27_out, xor_28_out);  // AND_Gate
  and and_61 (and_61_out, xor_27_out, ~xor_28_out);  // AND_Gate
  and and_62 (and_62_out, ~xor_29_out, xor_30_out);  // AND_Gate
  and and_63 (and_63_out, xor_29_out, ~xor_30_out);  // AND_Gate
  and and_64 (and_64_out, ~xor_31_out, xor_32_out);  // AND_Gate
  and and_65 (and_65_out, xor_31_out, ~xor_32_out);  // AND_Gate
  and and_66 (and_66_out, ~xor_33_out, xor_34_out);  // AND_Gate
  and and_67 (and_67_out, xor_33_out, ~xor_34_out);  // AND_Gate
  and and_68 (and_68_out, ~xor_35_out, xor_36_out);  // AND_Gate
  and and_69 (and_69_out, xor_35_out, ~xor_36_out);  // AND_Gate
  and and_70 (and_70_out, ~xor_37_out, xor_38_out);  // AND_Gate
  and and_71 (and_71_out, xor_37_out, ~xor_38_out);  // AND_Gate
  and and_72 (and_72_out, ~xor_39_out, xor_40_out);  // AND_Gate
  and and_73 (and_73_out, xor_39_out, ~xor_40_out);  // AND_Gate
  and and_74 (and_74_out, or_25_out, ~and_83_out);  // AND_Gate
  or or_25 (or_25_out, and_59_out, and_75_out);
  nor nor_2 (nor_2_out, and_58_out, and_59_out);
  and and_75 (and_75_out, or_26_out, ~and_84_out);  // AND_Gate
  or or_26 (or_26_out, and_61_out, and_76_out);
  nor nor_3 (nor_3_out, and_60_out, and_61_out);
  and and_76 (and_76_out, or_27_out, ~and_85_out);  // AND_Gate
  or or_27 (or_27_out, and_63_out, and_77_out);
  nor nor_4 (nor_4_out, and_62_out, and_63_out);
  and and_77 (and_77_out, or_28_out, ~and_86_out);  // AND_Gate
  or or_28 (or_28_out, and_65_out, and_78_out);
  nor nor_5 (nor_5_out, and_64_out, and_65_out);
  and and_78 (and_78_out, or_29_out, ~and_87_out);  // AND_Gate
  or or_29 (or_29_out, and_67_out, and_79_out);
  nor nor_6 (nor_6_out, and_66_out, and_67_out);
  and and_79 (and_79_out, or_30_out, ~and_88_out);  // AND_Gate
  or or_30 (or_30_out, and_69_out, and_80_out);
  nor nor_7 (nor_7_out, and_68_out, and_69_out);
  and and_80 (and_80_out, or_31_out, ~and_89_out);  // AND_Gate
  or or_31 (or_31_out, and_71_out, and_81_out);
  nor nor_8 (nor_8_out, and_70_out, and_71_out);
  and and_81 (and_81_out, or_32_out, ~pull_resistor_3_node);  // AND_Gate
  or or_32 (or_32_out, and_73_out, flags[1]);
  nor nor_9 (nor_9_out, and_72_out, and_73_out);
  Pull_Resistor pull_resistor_2 (.node(flags[1]));
  // AND_Gate and_82 has open pins: in0=or_33_out, in1=and_75_out, out=open
  or or_33 (or_33_out, and_58_out, and_83_out);
  and and_83 (and_83_out, or_34_out, ~and_76_out);  // AND_Gate
  or or_34 (or_34_out, and_60_out, and_84_out);
  and and_84 (and_84_out, or_35_out, ~and_77_out);  // AND_Gate
  or or_35 (or_35_out, and_62_out, and_85_out);
  and and_85 (and_85_out, or_36_out, ~and_78_out);  // AND_Gate
  or or_36 (or_36_out, and_64_out, and_86_out);
  and and_86 (and_86_out, or_37_out, ~and_79_out);  // AND_Gate
  or or_37 (or_37_out, and_66_out, and_87_out);
  and and_87 (and_87_out, or_38_out, ~and_80_out);  // AND_Gate
  or or_38 (or_38_out, and_68_out, and_88_out);
  and and_88 (and_88_out, or_39_out, ~and_81_out);  // AND_Gate
  or or_39 (or_39_out, and_70_out, and_89_out);
  and and_89 (and_89_out, or_40_out, ~flags[1]);  // AND_Gate
  or or_40 (or_40_out, and_72_out, pull_resistor_3_node);
  Pull_Resistor pull_resistor_3 (.node(pull_resistor_3_node));
  and and_90 (and_90_out, disable_AND___rotate, controlled_buffer_22_out);
  and and_91 (and_91_out, nor_9_out, nor_8_out, nor_7_out, nor_6_out, nor_5_out, nor_4_out, nor_3_out, nor_2_out);
  assign controlled_buffer_6_out[0] = inv_B___shit_direction ? A[1] : 1'bz;  // Controlled_Buffer controlled_buffer_6
  not not_3 (not_3_out, inv_B___shit_direction);
  assign controlled_buffer_6_out[0] = not_3_out ? and_90_out : 1'bz;  // Controlled_Buffer controlled_buffer_7
  assign controlled_buffer_6_out[1] = inv_B___shit_direction ? A[2] : 1'bz;  // Controlled_Buffer controlled_buffer_8
  not not_4 (not_4_out, inv_B___shit_direction);
  assign controlled_buffer_6_out[1] = not_4_out ? A[0] : 1'bz;  // Controlled_Buffer controlled_buffer_9
  assign controlled_buffer_6_out[2] = inv_B___shit_direction ? A[3] : 1'bz;  // Controlled_Buffer controlled_buffer_10
  not not_5 (not_5_out, inv_B___shit_direction);
  assign controlled_buffer_6_out[2] = not_5_out ? A[1] : 1'bz;  // Controlled_Buffer controlled_buffer_11
  assign controlled_buffer_6_out[3] = inv_B___shit_direction ? A[4] : 1'bz;  // Controlled_Buffer controlled_buffer_12
  not not_6 (not_6_out, inv_B___shit_direction);
  assign controlled_buffer_6_out[3] = not_6_out ? A[2] : 1'bz;  // Controlled_Buffer controlled_buffer_13
  assign controlled_buffer_6_out[4] = inv_B___shit_direction ? A[5] : 1'bz;  // Controlled_Buffer controlled_buffer_14
  not not_7 (not_7_out, inv_B___shit_direction);
  assign controlled_buffer_6_out[4] = not_7_out ? A[3] : 1'bz;  // Controlled_Buffer controlled_buffer_15
  assign controlled_buffer_6_out[5] = inv_B___shit_direction ? A[6] : 1'bz;  // Controlled_Buffer controlled_buffer_16
  not not_8 (not_8_out, inv_B___shit_direction);
  assign controlled_buffer_6_out[5] = not_8_out ? A[4] : 1'bz;  // Controlled_Buffer controlled_buffer_17
  assign controlled_buffer_6_out[6] = inv_B___shit_direction ? A[7] : 1'bz;  // Controlled_Buffer controlled_buffer_18
  not not_9 (not_9_out, inv_B___shit_direction);
  assign controlled_buffer_6_out[6] = not_9_out ? A[5] : 1'bz;  // Controlled_Buffer controlled_buffer_19
  assign controlled_buffer_6_out[7] = inv_B___shit_direction ? and_90_out : 1'bz;  // Controlled_Buffer controlled_buffer_20
  not not_10 (not_10_out, inv_B___shit_direction);
  assign controlled_buffer_6_out[7] = not_10_out ? A[6] : 1'bz;  // Controlled_Buffer controlled_buffer_21
  assign controlled_buffer_22_out = inv_B___shit_direction ? A[0] : 1'bz;  // Controlled_Buffer controlled_buffer_22
  not not_11 (not_11_out, inv_B___shit_direction);
  assign controlled_buffer_22_out = not_11_out ? A[7] : 1'bz;  // Controlled_Buffer controlled_buffer_23

  assign flags[0] = Cout;

  // Notes on the sheet:
  //   0: Cout, 1: Zero, 2: A over B, 3: A equals B
endmodule

module RAM_select_o_mat (
  input  auto,
  input  manual,
  input  [7:0] adress,
  input  [7:0] data,
  input  write,
  input  [7:0] manual_adress,
  input  manual_write,
  input  [7:0] manual_data,
  input  [7:0] ROM_data,
  input  load,
  output green_led_out,
  output red_led_out,
  output [7:0] ROM_adress,
  output write_out,
  output [7:0] adress_out,
  output [7:0] data_out,
  output load_clock
);

  wire and_1_out, buffer_1_out, buffer_2_out, buffer_3_out, clock_1_out, controlled_buffer_1_out,
       counter_1_carry, not_1_out, not_2_out, or_1_out, s_r_ff_1_q, s_r_ff_1_qn;
  wire [7:0] controlled_buffer_3_out, controlled_buffer_8_out;

  Clock clock_1 (.out(clock_1_out));
  S_R_Flip_Flop s_r_ff_1 (
    .S(load), .clk(clock_1_out), .R(counter_1_carry), .Q(s_r_ff_1_q), .Qn(s_r_ff_1_qn), .en(1'b1));  // open: preset, reset
  Counter #(.trigger("falling")) counter_1 (
    .count(s_r_ff_1_q), .Q(ROM_adress), .carry(counter_1_carry), .clk(clock_1_out), .clr(load));  // open: load, D
  assign controlled_buffer_1_out = red_led_out ? manual_write : 1'bz;  // Controlled_Buffer controlled_buffer_1
  not not_1 (not_1_out, s_r_ff_1_qn);
  not not_2 (not_2_out, s_r_ff_1_qn);
  and and_1 (and_1_out, not_2_out, clock_1_out);
  or or_1 (or_1_out, and_1_out, manual_write);
  buf buffer_1 (buffer_1_out, or_1_out);
  buf buffer_2 (buffer_2_out, buffer_1_out);
  buf buffer_3 (buffer_3_out, buffer_2_out);
  buf buffer_4 (load_clock, buffer_3_out);
  Pull_Resistor #(.pull(1)) pull_resistor_1 (.node(green_led_out));
  nor nor_1 (green_led_out, manual, red_led_out);
  Pull_Resistor pull_resistor_2 (.node(red_led_out));
  nor nor_2 (red_led_out, green_led_out, auto);
  assign controlled_buffer_1_out = green_led_out ? write : 1'bz;  // Controlled_Buffer controlled_buffer_2
  assign controlled_buffer_3_out = red_led_out ? manual_adress : 8'bz;  // Controlled_Buffer controlled_buffer_3
  assign write_out = not_1_out ? clock_1_out : 1'bz;  // Controlled_Buffer controlled_buffer_4
  assign write_out = s_r_ff_1_qn ? controlled_buffer_1_out : 1'bz;  // Controlled_Buffer controlled_buffer_5
  assign adress_out = not_1_out ? ROM_adress : 8'bz;  // Controlled_Buffer controlled_buffer_6
  assign controlled_buffer_3_out = green_led_out ? adress : 8'bz;  // Controlled_Buffer controlled_buffer_7
  assign controlled_buffer_8_out = red_led_out ? manual_data : 8'bz;  // Controlled_Buffer controlled_buffer_8
  assign data_out = not_1_out ? ROM_data : 8'bz;  // Controlled_Buffer controlled_buffer_9
  assign adress_out = s_r_ff_1_qn ? controlled_buffer_3_out : 8'bz;  // Controlled_Buffer controlled_buffer_10
  assign controlled_buffer_8_out = green_led_out ? data : 8'bz;  // Controlled_Buffer controlled_buffer_11
  assign data_out = s_r_ff_1_qn ? controlled_buffer_8_out : 8'bz;  // Controlled_Buffer controlled_buffer_12
endmodule

module _8_bit_enter_o_mat (
  input  in_1,
  input  in_2,
  input  in_3,
  input  in_4,
  input  in_5,
  input  in_6,
  input  in_7,
  input  in_8,
  input  in_9,
  output out_10,
  output out_11,
  output out_12,
  output out_13,
  output out_14,
  output out_15,
  output out_16,
  output out_17,
  output [7:0] out
);

  J_K_Flip_Flop j_k_ff_1 (.J(1'b1), .clk(in_1), .K(1'b1), .Q(out[7]), .en(1'b1), .reset(in_9));  // open: Qn, preset
  J_K_Flip_Flop j_k_ff_2 (.J(1'b1), .clk(in_2), .K(1'b1), .Q(out[6]), .en(1'b1), .reset(in_9));  // open: Qn, preset
  J_K_Flip_Flop j_k_ff_3 (.J(1'b1), .clk(in_3), .K(1'b1), .Q(out[5]), .en(1'b1), .reset(in_9));  // open: Qn, preset
  J_K_Flip_Flop j_k_ff_4 (.J(1'b1), .clk(in_4), .K(1'b1), .Q(out[4]), .en(1'b1), .reset(in_9));  // open: Qn, preset
  J_K_Flip_Flop j_k_ff_5 (.J(1'b1), .clk(in_5), .K(1'b1), .Q(out[3]), .en(1'b1), .reset(in_9));  // open: Qn, preset
  J_K_Flip_Flop j_k_ff_6 (.J(1'b1), .clk(in_6), .K(1'b1), .Q(out[2]), .en(1'b1), .reset(in_9));  // open: Qn, preset
  J_K_Flip_Flop j_k_ff_7 (.J(1'b1), .clk(in_7), .K(1'b1), .Q(out[1]), .en(1'b1), .reset(in_9));  // open: Qn, preset
  J_K_Flip_Flop j_k_ff_8 (.J(1'b1), .clk(in_8), .K(1'b1), .Q(out[0]), .en(1'b1), .reset(in_9));  // open: Qn, preset

  assign out_10 = out[7];
  assign out_11 = out[6];
  assign out_12 = out[5];
  assign out_13 = out[4];
  assign out_14 = out[3];
  assign out_15 = out[2];
  assign out_16 = out[1];
  assign out_17 = out[0];

  // Notes on the sheet:
  //   in_9: pull=down
endmodule

module _4_bit_enter_o_mat (
  input  in_1,
  input  in_2,
  input  in_3,
  input  in_4,
  output out_5,
  output out_6,
  output out_7,
  output out_8,
  output [3:0] out
);

  J_K_Flip_Flop j_k_ff_1 (.J(1'b1), .clk(in_1), .K(1'b1), .Q(out[3]), .en(1'b1));  // open: Qn, preset, reset
  J_K_Flip_Flop j_k_ff_2 (.J(1'b1), .clk(in_2), .K(1'b1), .Q(out[2]), .en(1'b1));  // open: Qn, preset, reset
  J_K_Flip_Flop j_k_ff_3 (.J(1'b1), .clk(in_3), .K(1'b1), .Q(out[1]), .en(1'b1));  // open: Qn, preset, reset
  J_K_Flip_Flop j_k_ff_4 (.J(1'b1), .clk(in_4), .K(1'b1), .Q(out[0]), .en(1'b1));  // open: Qn, preset, reset

  assign out_5 = out[3];
  assign out_6 = out[2];
  assign out_7 = out[1];
  assign out_8 = out[0];
endmodule
